# Fritzing sketch mcqueen (saved by Fritzing 0.8.7b)
circuit board: 8.46667cm x 5.64444cm
breadboards: 1

parts:
  Raspberry_Pi_B_rev1 = Raspberry Pi B rev2
  PWM1 = PCA9685 16x12-bit PWM Breakout

nets:
  N1: Raspberry_Pi_B_rev1.GPIO_2, PWM1.no_name_yet#504
  N2: Raspberry_Pi_B_rev1.GPIO_3, PWM1.no_name_yet#503
  N3: Raspberry_Pi_B_rev1.GND, PWM1.no_name_yet#501
  N4: Raspberry_Pi_B_rev1.GPIO_4, PWM1.no_name_yet#505
